# Fritzing sketch Prototype (saved by Fritzing 0.9.3b)
breadboards: 1

parts:
  Composant1 = Arduino Uno (Rev3)
  R1 = Resistor [tolerance=±5% resistance=100 package=THT]
  L1 = Inductor [inductance=10mH package="400 mil [THT]"]
  R2 = Resistor [tolerance=±5% resistance=1M package=THT]
  LED1 = LED - 5mm [color="Yellow (595nm)" package="5 mm [THT]"]
  R3 = Resistor [tolerance=±5% resistance=220 package=THT]
  LED2 = LED - 5mm [color="Green (555nm)" package="5 mm [THT]"]
  R4 = Resistor [tolerance=±5% resistance=220 package=THT]
  LED3 = LED - 5mm [color="Red (633nm)" package="5 mm [THT]"]
  R5 = Resistor [tolerance=±5% resistance=220 package=THT]

nets (from the schematic view):
  Patate: Composant1.A0, L1.pin_0, R2.Pin_1
  N1: Composant1.D9_PWM, R1.Pin_0
  N2: Composant1.GND, R2.Pin_0, LED1.cathode, LED2.cathode, LED3.cathode
  N3: Composant1.D5_PWM, R5.Pin_1
  N4: Composant1.D6_PWM, R4.Pin_0
  N5: Composant1.D7, R3.Pin_0
  N6: R1.Pin_1, L1.pin_1
  N7: LED1.anode, R4.Pin_1
  N8: R3.Pin_1, LED2.anode
  N9: LED3.anode, R5.Pin_0

// code stored in the sketch: Prototype.ino
//****************************************************************************************
// PWM Square Wave Generator
// VLO 2013-2014
//****************************************************************************************

int GetCas();
void pushValue(int value);
int* CopyThenBubbleSort(int* toCopy);
void setFrequency(float frequency);


const int outPin = 9; // output pin
const float maxFreq = 16000000; //max freq supported by Arduino (16MHz)

const int LED1 = 7;
const int LED2 = 6;
const int LED3 = 5;

const int width = 100; //nombre de valeur analys�es

int* values;

void setup()
{

  Serial.begin(115200); //for sending A0 pin values
  
  pinMode(outPin,OUTPUT);        //Signal generator pin
  pinMode(LED1,OUTPUT); 
  pinMode(LED2,OUTPUT); 
  pinMode(LED3,OUTPUT); 

  values = new int[width];
 
  
  setFrequency(350000); //generate a square wave 
  
  //for test
  //Serial.println();
  //Serial.println(ICR1);
  //Serial.println(TCCR1B);

  digitalWrite(LED1,HIGH);
  delay (200);
  digitalWrite(LED1,LOW);
  digitalWrite(LED2,HIGH);
  delay (200);
  digitalWrite(LED2,LOW);
  digitalWrite(LED3,HIGH);
  delay (200);
  digitalWrite(LED3,LOW);
  delay (100);
  digitalWrite(LED3,HIGH);
  delay (200);
  digitalWrite(LED3,LOW);
  digitalWrite(LED2,HIGH);
  delay (200);
  digitalWrite(LED2,LOW);
  digitalWrite(LED1,HIGH);
  delay (200);
  digitalWrite(LED1,LOW);
  digitalWrite(LED1,HIGH);
  digitalWrite(LED2,HIGH);
  digitalWrite(LED3,HIGH);
  delay (300);
}

void loop()
{


  int val = analogRead(0); 
  
  pushValue(val);  

  int cas = GetCas();

  switch(cas)
  {
    case 1: // 1 doigt
    digitalWrite(LED1,HIGH);
    digitalWrite(LED2,LOW);
    digitalWrite(LED3,LOW);
    break;

    case 2: // 2 doigts
    digitalWrite(LED1,LOW);
    digitalWrite(LED2,HIGH);
    digitalWrite(LED3,LOW);
    break;


    case 3: // main
    digitalWrite(LED1,LOW);
    digitalWrite(LED2,LOW);
    digitalWrite(LED3,HIGH);
    break;


    default:
    digitalWrite(LED1,LOW);
    digitalWrite(LED2,LOW);
    digitalWrite(LED3,LOW);
    break;
  }
  

                                 
  Serial.write( 0xff );                                                         
  Serial.write( (val >> 8) & 0xff );                                            
  Serial.write( val & 0xff );
 
}

//set frequency (Hz)
//min frequency: 0.24 Hz
//max frequency: 8MHz
void setFrequency(float frequency)
{
 
  if(frequency >=0.24 || frequency <=8000000)
  {
    
    TCCR1A=0b10000010;        // Set up frequency generator, mode 14 (Fast PWM)
    //WGM11 = 1, COM1A1 = 1
    //Fast PWM: TOP=ICR1, update of OCR1x=BOTTOM, TOV1 Flag Set on TOP
    
  
    unsigned int v=0;
    int indscale=0;
    float prescale[] = {1.0,8.0,64.0,256.0,1024.0};
    float period=1/frequency;
    
    while(v==0)
    {
      float curfreq=maxFreq/prescale[indscale];
      float tickperiod=1/curfreq;
      float nbtick=period/tickperiod;
     
      if(nbtick>65535)
      {
        indscale=indscale+1;
      }
      else
      {
        v=nbtick;
      }

    }
    
    int c=prescale[indscale];
    
     switch (c) {
      
         case 1: TCCR1B=0b00011001; break;
         case 8: TCCR1B=0b00011010; break;
         case 64: TCCR1B=0b00011011; break;
         case 256: TCCR1B=0b00011100; break;
         case 1024: TCCR1B=0b00011101; break;
         default: TCCR1B=0b00011000;
     }
    
    //WGM12 = 1, WGM13 = 1
    
    //three last bit of TCCR1B:    CS12   CS11   CS10
    // 0: no clock (timer stopped)  0      0      0
    // clk/1: no prescaling         0      0      1 
    // clk/8                        0      1      0
    // clk/64                       0      1      1
    // clk/256                      1      0      0
    // clk/1024                     1      0      1

    
    ICR1=v; //pulse duration = ICR1 value x time per counter tick
    
    //for 16Mhz (chip frequency)
    //Prescale	Time per counter tick
    //1	        0.0625 uS
    //8	        0.5 uS
    //64	4 uS
    //256	16 uS
    //1024	64uS
    
    OCR1A=v/2; //Output Compare Register //low state

  }
  
  
}


int GetCas()
{
  int* trier = CopyThenBubbleSort(values); //tri du tableau
  int crete = trier[width-1] - trier[0];
  delete trier;

 if(crete < ((1.70 * 1023.0) / 5))
    if(crete < ((0.70 * 1023.0) / 5))
        if(crete < ((0.61 * 1023.0) / 5))
          return 3;
        else 
        return 2;
    else 
    return 1;
  else 
  return 0;

 
}


void pushValue(int value)
{
  for (int i=0; i<width-1; i++)
    values[i] = values[i+1];
  values[width-1] = value;
}


int* CopyThenBubbleSort(int* toCopy)
{
  int *tab = new int[width];
    for(int i = 0; i<width ; i++)
    {
       tab[i] = toCopy[i];
    }

  int temp;
  for(int i = width-1; i>0; i--)
  {
      for(int j = 0; j<=i-1; j++)
      {
         if(tab[j+1] < tab[j])
         {
          temp = tab[j];
          tab[j] = tab[j+1];
          tab[j+1] = temp;
         
          }
        
        }
  
  }

  return tab;
}
